# Fritzing sketch Wiring (saved by Fritzing 0.9.3b)

parts:
  Part1 = Arduino Uno (Rev3)
  S1 = Pushbutton [package="[THT]"]
  J1 = female pin header, 3 pins [form="♀ (female)"]
  J3 = male pin header, 6 pins [form="♂ (male)"]
  J4 = male pin header, 6 pins [form="♂ (male)"]  # not connected

nets:
  N1: Part1.GND, S1.Pin_3, S1.Pin_4, J1.pin3
  N2: Part1.D2, S1.Pin_1, S1.Pin_2
  N3: Part1.D3_PWM, J3.pin5
  N4: Part1.D6_PWM, J1.pin2
  N5: Part1.5V, J1.pin1

notes:
  push button
  sleep indicator
  Halos cable, grey wire at top
